# Fritzing sketch Mapper85_DonkeyKongCountry4VRC7 (saved by Fritzing 1.0.3b)
circuit board: 9.00001cm x 5.68cm
breadboards: 1

parts:
  1-30 = Generic single row SMD female header - 30 pins [form="♀ (female)" package=THT]
  60-31 = Generic single row SMD female header - 30 pins [form="♀ (female)" package=THT]
  27C2 = 27C020 EEPROM [chip_label=27C020 package="DIP (Dual Inline) [THT]"]  # not connected
  3_58MHz = Crystal [frequency="16 Mhz" package=SMD]
  27C1 = 27C020 [chip_label=27C020]
  VRC7 = IC, DIP package, 48 pins [chip_label=IC]
  LM386 = LM 358 Dual Op-Amp [package="SO 08 [SMD]"]
  LM387 = LM 358 Dual Op-Amp [package="SO 08 [SMD]"]

nets:
  N1: 1-30.pin1, 27C1.connector15
  N2: 60-31.pin1, LM386.connector7, LM387.connector7
  N3: 3_58MHz.pin_0, VRC7.pin17
  N4: 3_58MHz.pin_1, VRC7.pin16

custom parts:
  Generic single row SMD female header - 30 pins: Generic single row SMD female header
  27C020 EEPROM: An EPROM (rarely EROM), or erasable programmable read-only memory, is a type of programmable read-only memory (PROM) chip that retains its data when its power supply is switched off.
